// Logisim project s-mips.circ as structural Verilog
module S_MIPS_Board (
  input  DESHABILITAR_DISPATCHER,
  output halt
);

  wire button_1_out, CLK, CS, d_ff_1_q, LCLR, LoadRAM, LoadRAMOn, LW, R_R_W, R_W, ram_dispatcher_1_finished,
       RCS, Reset_out, RST, TTY_EN;
  wire [2:0] KDB;
  wire [3:0] LMask, Mask, ram_1_read_time, ram_1_write_time, RMask;
  wire [6:0] KDB_DATA, TTY_DATA;
  wire [15:0] Addr, LAddr, RAddr;
  wire [31:0] I0, I1, I2, I3, LData, ram_1_data_out_0, ram_1_data_out_1, ram_1_data_out_2, ram_1_data_out_3,
       RI0, RI1, RI2, RI3;

  TTY #(.rows(25), .cols(80)) tty_1 (.data(TTY_DATA), .clk(CLK), .we(TTY_EN), .clr(RST));
  not not_1 (LoadRAMOn, ram_dispatcher_1_finished);
  RAM_Dispatcher ram_dispatcher_1 (
    .WriteTime(ram_1_write_time), .Clock(CLK), .Data(LData), .Address(LAddr), .Mask(LMask),
    .Finished(ram_dispatcher_1_finished), .Write(LW), .CLR(LCLR));
  Keyboard #(.buflen(64)) keyboard_1 (.clk(CLK), .re(KDB[0]), .avail(KDB[2]), .data(KDB_DATA));  // open: clr
  RAM ram_1 (
    .Address(RAddr), .Data_Out_0(ram_1_data_out_0), .Data_Out_1(ram_1_data_out_1),
    .Data_Out_2(ram_1_data_out_2), .Data_Out_3(ram_1_data_out_3), .Data_In_0(RI0), .Data_In_1(RI1),
    .Data_In_2(RI2), .Data_In_3(RI3), .Mask(RMask), .nRead_Write(R_R_W), .Chip_Select(RCS),
    .Read_Time(ram_1_read_time), .Reset(button_1_out), .Write_Time(ram_1_write_time));
  Button button_1 (.out(button_1_out));
  D_Flip_Flop d_ff_1 (.clk(CLK), .D(1'b1), .Q(d_ff_1_q), .reset(Reset_out));  // open: Qn, preset, en
  Button Reset (.out(Reset_out));
  S_MIPS s_mips_1 (
    .Kbd_Enable(KDB[0]), .Address(Addr), .Kbd_Clear(KDB[1]), .Kbd_Available(KDB[2]), .RAM_In_0(I0),
    .Kbd_ASCII_Data(KDB_DATA), .RAM_In_1(I1), .TTY_Enable(TTY_EN), .RAM_In_2(I2), .RAM_In_3(I3),
    .TTY_ASCII_Data(TTY_DATA), .Reset(RST), .RAM_Out_0(ram_1_data_out_0), .Clock(CLK),
    .RAM_Out_1(ram_1_data_out_1), .Stop(halt), .RAM_Out_2(ram_1_data_out_2), .RAM_Out_3(ram_1_data_out_3),
    .Mask(Mask), .Read_Time(ram_1_read_time), .Write_Time(ram_1_write_time), .nRead_Write(R_W),
    .Chip_Select(CS));
  D_Flip_Flop d_ff_2 (.clk(CLK), .D(d_ff_1_q), .Qn(LCLR), .reset(Reset_out));  // open: Q, preset, en
  or or_1 (RST, LCLR, LoadRAM);
  Clock clock_1 (.out(CLK));
  Multiplexer #(.width(32), .enable("false")) multiplexer_1 (.in0(I0), .in1(LData), .out(RI0), .sel(LoadRAM));
  Multiplexer #(.width(32), .enable("false")) multiplexer_2 (.in0(I1), .in1(LData), .out(RI1), .sel(LoadRAM));
  Multiplexer #(.width(32), .enable("false")) multiplexer_3 (.in0(I2), .in1(LData), .out(RI2), .sel(LoadRAM));
  Multiplexer #(.width(32), .enable("false")) multiplexer_4 (.in0(I3), .in1(LData), .out(RI3), .sel(LoadRAM));
  and and_1 (LoadRAM, ~DESHABILITAR_DISPATCHER, LoadRAMOn);  // AND_Gate
  Multiplexer #(.width(16), .enable("false")) multiplexer_5 (.in0(Addr), .in1(LAddr), .out(RAddr), .sel(LoadRAM));
  Multiplexer #(.width(4), .enable("false")) multiplexer_6 (.in0(Mask), .in1(LMask), .out(RMask), .sel(LoadRAM));
  Multiplexer #(.enable("false")) multiplexer_7 (.in0(CS), .in1(LW), .out(RCS), .sel(LoadRAM));
  Multiplexer #(.enable("false")) multiplexer_8 (.in0(R_W), .in1(LW), .out(R_R_W), .sel(LoadRAM));

  // Notes on the sheet:
  //   NO MODIFICAR
  //   Keyboard
endmodule

module RAM (
  input  [15:0] Address,
  input  [31:0] Data_In_0,
  input  [31:0] Data_In_1,
  input  [31:0] Data_In_2,
  input  [31:0] Data_In_3,
  input  [3:0] Mask,
  input  nRead_Write,
  input  Chip_Select,
  input  Reset,
  output [31:0] Data_Out_0,
  output [31:0] Data_Out_1,
  output [31:0] Data_Out_2,
  output [31:0] Data_Out_3,
  output [3:0] Read_Time,
  output [3:0] Write_Time
);

  wire and_2_out, and_3_out, and_4_out, and_5_out, and_6_out, and_7_out, and_8_out, and_9_out, Changed, CLK,
       comparator_2_eq, comparator_3_eq, comparator_4_eq, comparator_5_eq, comparator_6_eq, Count,
       demultiplexer_3_out0, Idle, Idle_q, Load, Load0, Load1, nand_1_out, or_1_out, or_2_out, or_3_out,
       or_4_out, or_5_out, or_6_out, or_7_out, or_8_out, or_9_out, or_10_out, Proc_q, Update_Mem, Zero_Time;
  wire [3:0] counter_1_q, multiplexer_1_out, subtractor_1_out;
  wire [31:0] register_1_q, register_2_q, register_3_q, register_4_q, register_5_q;

  // Probe on 4'b0011
  // Probe on 4'b0010
  Multiplexer #(.width(4), .enable("false")) multiplexer_1 (
    .in0(4'b0011), .in1(4'b0010), .out(multiplexer_1_out), .sel(nRead_Write));
  or or_1 (or_1_out, Idle, Update_Mem);
  or or_2 (or_2_out, ~Chip_Select, Reset);  // OR_Gate
  Subtractor #(.width(4)) subtractor_1 (.a(multiplexer_1_out), .b(4'b0010), .out(subtractor_1_out));  // open: bin, bout
  Demultiplexer #(.enable("false")) demultiplexer_1 (.out0(Idle), .out1(Load0), .in(Idle_q), .sel(Changed));
  D_Flip_Flop u_Idle (.clk(CLK), .D(or_1_out), .Q(Idle_q), .preset(or_2_out));  // open: Qn, en, reset
  // Probe on counter_1_q
  Counter #(.width(4), .max('hf)) counter_1 (
    .load(Load), .D(subtractor_1_out), .count(Count), .Q(counter_1_q), .clk(CLK), .clr(or_3_out));  // open: carry
  or or_3 (or_3_out, ~Chip_Select, Reset);  // OR_Gate
  Comparator_part #(.width(4), .mode("unsigned")) comparator_1 (
    .a(4'b0000), .b(counter_1_q), .eq(Zero_Time));  // open: gt, lt
  or or_4 (or_4_out, Count, Load0, Load1);
  Register #(.width(32)) register_1 (.D(Data_In_0), .en(Chip_Select), .Q(register_1_q), .clk(CLK), .clr(or_5_out));
  or or_5 (or_5_out, ~Chip_Select, Reset);  // OR_Gate
  Register #(.width(32)) register_2 (.D(Data_In_1), .en(Chip_Select), .Q(register_2_q), .clk(CLK), .clr(or_6_out));
  or or_6 (or_6_out, ~Chip_Select, Reset);  // OR_Gate
  Register #(.width(32)) register_3 (.D(Data_In_2), .en(Chip_Select), .Q(register_3_q), .clk(CLK), .clr(or_7_out));
  or or_7 (or_7_out, ~Chip_Select, Reset);  // OR_Gate
  Register #(.width(32)) register_4 (.D(Data_In_3), .en(Chip_Select), .Q(register_4_q), .clk(CLK), .clr(or_8_out));
  or or_8 (or_8_out, ~Chip_Select, Reset);  // OR_Gate
  Register #(.width(32)) register_5 (
    .D({{11{1'b1}}, nRead_Write, Mask, Address}), .en(Chip_Select), .Q(register_5_q), .clk(CLK),
    .clr(or_9_out));
  or or_9 (or_9_out, ~Chip_Select, Reset);  // OR_Gate
  D_Flip_Flop Proc (.clk(CLK), .D(or_4_out), .Q(Proc_q), .reset(or_10_out));  // open: Qn, preset, en
  or or_10 (or_10_out, ~Chip_Select, Reset);  // OR_Gate
  Demultiplexer #(.enable("false")) demultiplexer_2 (
    .out0(Count), .out1(Update_Mem), .in(demultiplexer_3_out0), .sel(Zero_Time));
  Demultiplexer #(.enable("false")) demultiplexer_3 (
    .out0(demultiplexer_3_out0), .out1(Load1), .in(Proc_q), .sel(Changed));
  Clock clock_1 (.out(CLK));
  Comparator_part #(.width(32)) comparator_2 (.a(register_1_q), .b(Data_In_0), .eq(comparator_2_eq));  // open: gt, lt
  Comparator_part #(.width(32)) comparator_3 (.a(register_2_q), .b(Data_In_1), .eq(comparator_3_eq));  // open: gt, lt
  Comparator_part #(.width(32)) comparator_4 (.a(register_3_q), .b(Data_In_2), .eq(comparator_4_eq));  // open: gt, lt
  Comparator_part #(.width(32)) comparator_5 (.a(register_4_q), .b(Data_In_3), .eq(comparator_5_eq));  // open: gt, lt
  Comparator_part #(.width(32)) comparator_6 (
    .a(register_5_q), .b({{11{1'b1}}, nRead_Write, Mask, Address}), .eq(comparator_6_eq));  // open: gt, lt
  nand nand_1 (nand_1_out, comparator_6_eq, comparator_2_eq, comparator_3_eq, comparator_4_eq, comparator_5_eq);
  and and_1 (Changed, nand_1_out, Chip_Select);
  or or_11 (Load, Count, Load1, Load0);
  and and_2 (and_2_out, Mask[0], Update_Mem, nRead_Write);
  and and_3 (and_3_out, Mask[1], Update_Mem, nRead_Write);
  and and_4 (and_4_out, Mask[2], Update_Mem, nRead_Write);
  and and_5 (and_5_out, Mask[3], Update_Mem, nRead_Write);
  RAM_part #(.addrWidth(16), .dataWidth(32), .bus("separate")) ram_1 (
    .addr(Address), .din(Data_In_0), .data(Data_Out_0), .str(and_2_out), .sel(Chip_Select), .clk(CLK),
    .ld(and_6_out), .clr(Reset));
  and and_6 (and_6_out, ~nRead_Write, Idle);  // AND_Gate
  RAM_part #(.addrWidth(16), .dataWidth(32), .bus("separate")) ram_2 (
    .addr(Address), .din(Data_In_1), .data(Data_Out_1), .str(and_3_out), .sel(Chip_Select), .clk(CLK),
    .ld(and_7_out), .clr(Reset));
  and and_7 (and_7_out, ~nRead_Write, Idle);  // AND_Gate
  RAM_part #(.addrWidth(16), .dataWidth(32), .bus("separate")) ram_3 (
    .addr(Address), .din(Data_In_2), .data(Data_Out_2), .str(and_4_out), .sel(Chip_Select), .clk(CLK),
    .ld(and_8_out), .clr(Reset));
  and and_8 (and_8_out, ~nRead_Write, Idle);  // AND_Gate
  RAM_part #(.addrWidth(16), .dataWidth(32), .bus("separate")) ram_4 (
    .addr(Address), .din(Data_In_3), .data(Data_Out_3), .str(and_5_out), .sel(Chip_Select), .clk(CLK),
    .ld(and_9_out), .clr(Reset));
  and and_9 (and_9_out, ~nRead_Write, Idle);  // AND_Gate

  assign Read_Time = 4'b0011;
  assign Write_Time = 4'b0010;

  // Other names for the same wires on the sheet: M0 = Mask[0]; M1 = Mask[1]; M2 = Mask[2]; M3 = Mask[3];
  //   RW = nRead_Write; CLR = Reset; CS = Chip_Select; Load2 = Count

  // Notes on the sheet:
  //   NO MODIFICAR
  //   excepto quizás los valores RT y WT
  //   BANK0
  //   BANK1
  //   BANK2
  //   BANK3
endmodule

module RAM_Dispatcher (
  input  [3:0] WriteTime,
  input  Clock,
  input  CLR,
  output [31:0] Data,
  output [15:0] Address,
  output [3:0] Mask,
  output Finished,
  output Write
);

  wire demultiplexer_2_out1, demultiplexer_3_out1, End, IDLE_q, IncAddr, Load, or_1_out, or_2_out, While_q,
       WriteEnd;
  wire [3:0] counter_1_q;
  wire [31:0] CurrentAddress_q;

  Counter #(.width(32), .max('hffffffff)) CurrentAddress (
    .count(IncAddr), .Q({CurrentAddress_q[31:18], Address, CurrentAddress_q[1:0]}), .clk(Clock), .clr(CLR));  // open: load, D, carry
  or or_1 (or_1_out, IncAddr, demultiplexer_3_out1, Finished);
  D_Flip_Flop IDLE (.clk(Clock), .D(or_1_out), .Q(IDLE_q), .preset(CLR));  // open: Qn, en, reset
  Demultiplexer #(.enable("false")) demultiplexer_1 (.out0(Load), .out1(Finished), .in(IDLE_q), .sel(End));
  D_Flip_Flop While (.clk(Clock), .D(or_2_out), .Q(While_q), .reset(CLR));  // open: Qn, preset, en
  or or_2 (or_2_out, Write, Load);
  RAM_part #(.addrWidth(18), .dataWidth(32)) ram_1 (
    .addr({Address, CurrentAddress_q[1:0]}), .data(Data), .clk(Clock));  // open: sel, ld, clr
  Demultiplexer #(.enable("false")) demultiplexer_2 (
    .out0(Write), .out1(demultiplexer_2_out1), .in(While_q), .sel(WriteEnd));
  Decoder #(.select(2)) decoder_1 (
    .out0(Mask[0]), .out1(Mask[1]), .out2(Mask[2]), .out3(Mask[3]), .sel(CurrentAddress_q[1:0]));  // open: en
  Demultiplexer #(.enable("false")) demultiplexer_3 (
    .out0(IncAddr), .out1(demultiplexer_3_out1), .in(demultiplexer_2_out1), .sel(End));
  Counter #(.width(4), .max('hf)) counter_1 (
    .load(Load), .D(WriteTime), .count(Write), .Q(counter_1_q), .clk(Clock));  // open: carry, clr
  Comparator_part #(.width(32)) comparator_1 (.a(Data), .b({32{1'b1}}), .eq(End));  // open: gt, lt
  Comparator_part #(.width(4)) comparator_2 (.a(4'b0000), .b(counter_1_q), .eq(WriteEnd));  // open: gt, lt

  // Other names for the same wires on the sheet: CLK = Clock; Count = Write; WT[3:0] = WriteTime
endmodule

module S_MIPS (
  input  Kbd_Available,
  input  [6:0] Kbd_ASCII_Data,
  input  [31:0] RAM_Out_0,
  input  [31:0] RAM_Out_1,
  input  Reset,
  input  [31:0] RAM_Out_2,
  input  Clock,
  input  [31:0] RAM_Out_3,
  input  [3:0] Read_Time,
  input  [3:0] Write_Time,
  output Kbd_Enable,
  output [15:0] Address,
  output Kbd_Clear,
  output TTY_Enable,
  output [6:0] TTY_ASCII_Data,
  output Stop,
  output [31:0] RAM_In_0,
  output [31:0] RAM_In_1,
  output [31:0] RAM_In_2,
  output [31:0] RAM_In_3,
  output [3:0] Mask,
  output nRead_Write,
  output Chip_Select
);

  wire d_ff_1_q, Get_D, Get_I, INSTen, PCen, Ready_Data, Ready_Inst, Ready_Write, RegW, SPen, START, startEN,
       Write_D;
  wire [5:0] Func, Op;
  wire [31:0] bit_extender_1_out, Instruction, multiplexer_1_out, Target;

  assign bit_extender_1_out = {{25{1'b0}}, Kbd_ASCII_Data};  // Bit_Extender bit_extender_1
  D_Flip_Flop #(.trigger("falling")) d_ff_1 (
    .clk(Clock), .D(1'b0), .Q(d_ff_1_q), .preset(Reset));  // open: Qn, en, reset
  Multiplexer #(.width(32)) multiplexer_1 (
    .in0({32{1'b1}}), .in1(bit_extender_1_out), .out(multiplexer_1_out), .sel(Kbd_Available));  // open: en
  D_Flip_Flop #(.trigger("falling")) d_ff_2 (
    .clk(Clock), .D(d_ff_1_q), .Q(START), .reset(Reset));  // open: Qn, preset, en
  Control_Unit control_unit_1 (
    .in_1(START), .in_2(Clock), .in_3(Reset), .in_4(Ready_Inst), .in_5(Ready_Data), .in_6(Ready_Write),
    .in_7(Op), .in_8(Func), .Get_Inst(Get_I), .PCen(PCen), .SPen(SPen), .INSTen(INSTen), .KBDen(Kbd_Enable),
    .RegW(RegW), .TTYen(TTY_Enable), .WriteD(Write_D), .startEN(startEN), .End(Stop), .Get_Data(Get_D));
  Data_Path data_path_1 (
    .in_1(Instruction), .in_2(multiplexer_1_out), .in_3(Clock), .in_4(Reset), .in_5(PCen), .in_6(INSTen),
    .in_7(Kbd_Enable), .in_8(startEN), .Memory_Address(Target), .TTY_Data(TTY_ASCII_Data),
    .Data_RAM(RAM_In_0), .in_9(RegW), .Op_code(Op), .Func_code(Func), .in_10(SPen));
  RAM_Access ram_access_1 (
    .in_1(Target), .in_2(RAM_Out_0), .in_3(RAM_Out_1), .in_4(RAM_Out_2), .in_5(RAM_Out_3), .Address(Address),
    .Mask(Mask), .RAM_Out(Instruction), .in_6(Read_Time), .in_7(Write_Time), .in_8(Write_D), .in_9(Clock),
    .in_10(Reset), .in_11(Get_I), .in_12(Get_D), .R_W(nRead_Write), .Chip_Select(Chip_Select),
    .Ready_Instruction(Ready_Inst), .Ready_Data(Ready_Data), .Ready_Write(Ready_Write), .in_13(INSTen));

  assign Kbd_Clear = Reset;
  assign RAM_In_1 = RAM_In_0;
  assign RAM_In_2 = RAM_In_0;
  assign RAM_In_3 = RAM_In_0;

  // Other names for the same wires on the sheet: CLK = Clock; CS = Chip_Select; KBD_AVAIL = Kbd_Available;
  //   CLR = Reset; KBD_CLR = Reset; KBD_DATA[6:0] = Kbd_ASCII_Data; KBDen = Kbd_Enable; RAM_A[15:0] = Address;
  //   Data_RAM[31:0] = RAM_In_0; RAM_INPUT_0[31:0] = RAM_In_0; RAM_INPUT_1[31:0] = RAM_In_0;
  //   RAM_INPUT_2[31:0] = RAM_In_0; RAM_INPUT_3[31:0] = RAM_In_0; RAM_MASK[3:0] = Mask;
  //   RAM_OUTPUT_0[31:0] = RAM_Out_0; RAM_OUTPUT_1[31:0] = RAM_Out_1; RAM_OUTPUT_2[31:0] = RAM_Out_2;
  //   RAM_OUTPUT_3[31:0] = RAM_Out_3; RW = nRead_Write; TTY_DATA[6:0] = TTY_ASCII_Data

  // Notes on the sheet:
  //   RAM ADDRESS
  //   DATA FROM RAM
  //   DATA TO RAM
  //   DATA WRITE MASK
  //   RAM TIMING
  //   RAM CONTROL
  //   KEYBOARD
  //   TTY
  //   SEQUENCING
endmodule

module Control_Unit (
  input  in_1,
  input  in_2,
  input  in_3,
  input  in_4,
  input  in_5,
  input  in_6,
  input  [5:0] in_7,
  input  [5:0] in_8,
  output Get_Inst,
  output PCen,
  output SPen,
  output INSTen,
  output KBDen,
  output RegW,
  output TTYen,
  output WriteD,
  output startEN,
  output Get_Data,
  output End
);

  wire Alu, Cpy, demultiplexer_1_out0, demultiplexer_2_out0, demultiplexer_3_out0, demultiplexer_4_out0,
       demultiplexer_4_out1, halt, IDLE_q, Jmp, kbd, lw, Mry, operations_on_registers_decoder_1_halt,
       operations_on_registers_decoder_1_kbd, operations_on_registers_decoder_1_lw,
       operations_on_registers_decoder_1_pop, operations_on_registers_decoder_1_push,
       operations_on_registers_decoder_1_rnd, operations_on_registers_decoder_1_sw,
       operations_on_registers_decoder_1_tty, or_1_out, or_2_out, or_4_out, or_6_out, pop, push, rnd, Spc,
       SPen1, SPen2, startEN_t, sw, Wait_3_q, Wait_4_q, Wait_5_q, Wait_q;

  D_Flip_Flop #(.trigger("falling")) Wait (.clk(in_2), .D(Mry), .Q(Wait_q), .reset(in_3));  // open: Qn, preset, en
  or or_1 (or_1_out, Alu, in_5, rnd, Cpy, kbd);
  Demultiplexer demultiplexer_1 (
    .out0(demultiplexer_1_out0), .out1(Get_Data), .in(Wait_q), .sel(or_2_out));  // open: en
  or or_2 (or_2_out, lw, pop);
  D_Flip_Flop #(.trigger("falling")) Wait_2 (.clk(in_2), .D(or_1_out), .Q(RegW), .reset(in_3));  // open: Qn, preset, en
  Demultiplexer demultiplexer_2 (
    .out0(demultiplexer_2_out0), .out1(SPen1), .in(demultiplexer_1_out0), .sel(push));  // open: en
  Operation_Type operation_type_1 (
    .in_1(in_7), .in_2(in_8), .Cpy(Cpy), .Jmp(Jmp), .Mry(Mry), .Spc(Spc), .Alu(Alu), .in_3(startEN_t));
  D_Flip_Flop #(.trigger("falling")) d_ff_1 (
    .clk(in_2), .Q(startEN), .preset(startEN_t), .reset(PCen));  // open: D, Qn, en
  D_Flip_Flop #(.trigger("falling")) Wait_3 (.clk(in_2), .D(RegW), .Q(Wait_3_q), .reset(in_3));  // open: Qn, preset, en
  Demultiplexer demultiplexer_3 (.out0(demultiplexer_3_out0), .out1(SPen2), .in(Wait_3_q), .sel(pop));  // open: en
  or or_3 (WriteD, demultiplexer_2_out0, Wait_4_q);
  D_Flip_Flop #(.trigger("falling")) Wait_4 (
    .clk(in_2), .D(SPen1), .Q(Wait_4_q), .reset(in_3));  // open: Qn, preset, en
  and and_1 (KBDen, kbd, demultiplexer_3_out0);
  and and_2 (TTYen, startEN, operations_on_registers_decoder_1_tty);
  and and_3 (rnd, startEN, operations_on_registers_decoder_1_rnd);
  and and_4 (lw, startEN, operations_on_registers_decoder_1_lw);
  and and_5 (halt, startEN, operations_on_registers_decoder_1_halt);
  D_Flip_Flop #(.trigger("falling")) Wait_5 (
    .clk(in_2), .D(SPen2), .Q(Wait_5_q), .reset(in_3));  // open: Qn, preset, en
  and and_6 (kbd, startEN, operations_on_registers_decoder_1_kbd);
  Operations_on_Registers_Decoder operations_on_registers_decoder_1 (
    .in_1(in_7), .in_2(in_8), .pop(operations_on_registers_decoder_1_pop),
    .push(operations_on_registers_decoder_1_push), .lw(operations_on_registers_decoder_1_lw),
    .sw(operations_on_registers_decoder_1_sw), .tty(operations_on_registers_decoder_1_tty),
    .rnd(operations_on_registers_decoder_1_rnd), .kbd(operations_on_registers_decoder_1_kbd),
    .halt(operations_on_registers_decoder_1_halt));  // open: mfhi, mflo
  and and_7 (sw, startEN, operations_on_registers_decoder_1_sw);
  and and_8 (push, startEN, operations_on_registers_decoder_1_push);
  and and_9 (pop, operations_on_registers_decoder_1_pop, startEN);
  D_Flip_Flop #(.trigger("falling")) IDLE (
    .clk(in_2), .D(demultiplexer_4_out0), .Q(IDLE_q), .preset(in_3));  // open: Qn, en, reset
  Demultiplexer demultiplexer_4 (
    .out0(demultiplexer_4_out0), .out1(demultiplexer_4_out1), .in(IDLE_q), .sel(in_1));  // open: en
  or or_4 (or_4_out, Jmp, demultiplexer_3_out0, in_6, Wait_5_q, TTYen);
  D_Flip_Flop #(.trigger("falling")) Wait_6 (
    .clk(in_2), .D(in_4), .Q(startEN_t), .reset(in_3));  // open: Qn, preset, en
  or or_5 (Get_Inst, demultiplexer_4_out1, PCen);
  D_Flip_Flop #(.trigger("falling")) IDLE_2 (.clk(in_2), .D(or_4_out), .Q(PCen), .reset(in_3));  // open: Qn, preset, en
  or or_6 (or_6_out, End, halt);
  or or_7 (SPen, SPen1, SPen2);
  D_Flip_Flop #(.trigger("falling")) Wait_7 (.clk(in_2), .D(or_6_out), .Q(End), .reset(in_3));  // open: Qn, preset, en

  assign INSTen = in_4;

  // Other names for the same wires on the sheet: CLK = in_2; EN = startEN; Func_code[5:0] = in_8; Get_D = Get_Data;
  //   Op_code[5:0] = in_7; Ready_Data = in_5; Ready_Inst = in_4; Ready_Write = in_6; RST = in_3; START = in_1;
  //   stopEN = PCen; tty = TTYen; Write_Data = WriteD
endmodule

module Operation_Type (
  input  [5:0] in_1,
  input  [5:0] in_2,
  input  in_3,
  output Alu,
  output Cpy,
  output Jmp,
  output Mry,
  output Spc
);

  wire Alu_t, and_1_out, and_2_out, and_3_out, and_4_out, comparator_1_eq, comparator_2_eq, comparator_3_eq,
       comparator_4_eq, comparator_5_eq, comparator_6_eq, comparator_7_lt, comparator_8_eq, comparator_9_eq,
       comparator_10_eq, Cpy_t, I, J, Jmp_t, Mry_t, or_1_out, R, Spc_t;

  Operation_code operation_code_1 (.in_1(in_1), .R(R), .I(I), .J(J));
  Comparator_part #(.width(6)) comparator_1 (.a(in_1), .b({6{1'b0}}), .eq(comparator_1_eq));  // open: gt, lt
  and and_1 (and_1_out, comparator_1_eq, comparator_2_eq);
  Comparator_part #(.width(6)) comparator_2 (.a(in_2), .b(6'b010010), .eq(comparator_2_eq));  // open: gt, lt
  and and_2 (and_2_out, comparator_1_eq, comparator_3_eq);
  Comparator_part #(.width(6)) comparator_3 (.a(in_2), .b(6'b010000), .eq(comparator_3_eq));  // open: gt, lt
  Comparator_part #(.width(6)) comparator_4 (.a(in_1), .b({6{1'b0}}), .eq(comparator_4_eq));  // open: gt, lt
  Comparator_part #(.width(6)) comparator_5 (.a(in_2), .b({6{1'b0}}), .eq(comparator_5_eq));  // open: gt, lt
  or or_1 (or_1_out, comparator_5_eq, comparator_6_eq);
  Comparator_part #(.width(6)) comparator_6 (.a(in_2), .b(6'b001000), .eq(comparator_6_eq));  // open: gt, lt
  Comparator_part #(.width(6)) comparator_7 (.a(in_1), .b(6'b001000), .lt(comparator_7_lt));  // open: gt, eq
  Comparator_part #(.width(6)) comparator_8 (.a(in_1), .b(6'b111000), .eq(comparator_8_eq));  // open: gt, lt
  or or_2 (Mry_t, comparator_8_eq, comparator_9_eq, comparator_10_eq);
  Comparator_part #(.width(6)) comparator_9 (.a(in_1), .b(6'b100011), .eq(comparator_9_eq));  // open: gt, lt
  Comparator_part #(.width(6)) comparator_10 (.a(in_1), .b(6'b101011), .eq(comparator_10_eq));  // open: gt, lt
  Comparator_part #(.width(6)) comparator_11 (.a(in_1), .b({6{1'b1}}), .eq(Spc_t));  // open: gt, lt
  nor nor_1 (Alu_t, Cpy_t, Jmp_t, Mry_t, Spc_t);
  or or_3 (Cpy_t, and_1_out, and_2_out);
  and and_3 (and_3_out, comparator_4_eq, or_1_out);
  and and_4 (and_4_out, I, comparator_7_lt);
  or or_4 (Jmp_t, and_3_out, and_4_out);
  and and_5 (Alu, in_3, Alu_t);
  and and_6 (Cpy, in_3, Cpy_t);
  and and_7 (Jmp, in_3, Jmp_t);
  and and_8 (Mry, in_3, Mry_t);
  and and_9 (Spc, in_3, Spc_t);

  // Other names for the same wires on the sheet: EN = in_3; Func_code[5:0] = in_2; Op_code[5:0] = in_1
endmodule

module Data_Path (
  input  [31:0] in_1,
  input  [31:0] in_2,
  input  in_3,
  input  in_4,
  input  in_5,
  input  in_6,
  input  in_7,
  input  in_8,
  input  in_9,
  input  in_10,
  output [31:0] Memory_Address,
  output [31:0] Data_RAM,
  output [6:0] TTY_Data,
  output [5:0] Op_code,
  output [5:0] Func_code
);

  wire halt, I, J, kbd, LHiLo, lw, mfhi, mflo, operations_on_registers_decoder_1_halt,
       operations_on_registers_decoder_1_kbd, operations_on_registers_decoder_1_lw,
       operations_on_registers_decoder_1_mfhi, operations_on_registers_decoder_1_mflo,
       operations_on_registers_decoder_1_pop, operations_on_registers_decoder_1_push,
       operations_on_registers_decoder_1_rnd, operations_on_registers_decoder_1_sw,
       operations_on_registers_decoder_1_tty, or_1_out, or_2_out, or_3_out, pop, push, R, rnd, sw, tty;
  wire [4:0] multiplexer_3_out, Rd, Rs, Rt;
  wire [15:0] Cst;
  wire [25:0] Destine;
  wire [31:0] A, ALU_R, B, Hi, Hi_in, Lo, Lo_in, multiplexer_1_out, multiplexer_2_out, PC, PC_star, SP;

  Program_Counter program_counter_1 (.PC_star(PC_star), .in_2(in_3), .in_3(in_4), .in_4(in_5), .PC(PC));
  Branch_Control branch_control_1 (
    .in_1(PC), .in_2(A), .in_3(B), .in_4(Cst), .in_5(Destine), .in_6(Op_code), .in_7(Func_code),
    .Next_Instruction_Address(PC_star));
  Operation_code operation_code_1 (.in_1(Op_code), .R(R), .I(I), .J(J));
  and and_1 (rnd, in_8, operations_on_registers_decoder_1_rnd);
  and and_2 (tty, in_8, operations_on_registers_decoder_1_tty);
  and and_3 (lw, in_8, operations_on_registers_decoder_1_lw);
  and and_4 (halt, in_8, operations_on_registers_decoder_1_halt);
  Instruction_Decoder instruction_decoder_1 (
    .Instruction(in_1), .Op_code(Op_code), .Rs(Rs), .Rt(Rt), .Rd(Rd), .Func_code(Func_code), .Constante(Cst),
    .Destino_Salto(Destine), .in_3(in_3), .in_4(in_4), .in_2(in_6));
  and and_5 (kbd, in_8, operations_on_registers_decoder_1_kbd);
  Operations_on_Registers_Decoder operations_on_registers_decoder_1 (
    .in_1(Op_code), .in_2(Func_code), .mfhi(operations_on_registers_decoder_1_mfhi),
    .mflo(operations_on_registers_decoder_1_mflo), .pop(operations_on_registers_decoder_1_pop),
    .push(operations_on_registers_decoder_1_push), .lw(operations_on_registers_decoder_1_lw),
    .sw(operations_on_registers_decoder_1_sw), .tty(operations_on_registers_decoder_1_tty),
    .rnd(operations_on_registers_decoder_1_rnd), .kbd(operations_on_registers_decoder_1_kbd),
    .halt(operations_on_registers_decoder_1_halt));
  and and_6 (sw, in_8, operations_on_registers_decoder_1_sw);
  or or_1 (or_1_out, lw, pop);
  and and_7 (mfhi, operations_on_registers_decoder_1_mfhi, in_8);
  and and_8 (mflo, in_8, operations_on_registers_decoder_1_mflo);
  and and_9 (push, operations_on_registers_decoder_1_push, in_8);
  and and_10 (pop, in_8, operations_on_registers_decoder_1_pop);
  Multiplexer #(.width(32)) multiplexer_1 (
    .in0(ALU_R), .in1(in_1), .out(multiplexer_1_out), .sel(or_1_out));  // open: en
  Multiplexer #(.width(32)) multiplexer_2 (
    .in0(multiplexer_1_out), .in1(in_2), .out(multiplexer_2_out), .sel(in_7));  // open: en
  Multiplexer #(.width(5)) multiplexer_3 (.in0(Rd), .in1(Rt), .out(multiplexer_3_out), .sel(I));  // open: en
  or or_2 (or_2_out, push, pop);
  Memory_Address memory_address_1 (
    .in_1(PC), .in_2(SP), .in_3(ALU_R), .in_4(or_2_out), .in_5(or_3_out), .Memory_Address(Memory_Address));
  or or_3 (or_3_out, lw, sw);
  Register_File register_file_1 (
    .in_1(multiplexer_2_out), .in_2(multiplexer_3_out), .in_3(Rs), .in_4(Rt), .in_5(Hi_in), .in_6(Lo_in),
    .in_7(in_9), .in_8(mfhi), .in_9(mflo), .in_10(push), .in_11(pop), .in_12(rnd), .in_13(LHiLo),
    .in_14(in_3), .in_15(in_4), .A(A), .B(B), .Hi(Hi), .Lo(Lo), .SP(SP), .in_16(in_10));
  Multiplexer #(.width(32)) multiplexer_4 (
    .in0(A), .in1(B), .out({Data_RAM[7:0], Data_RAM[15:8], Data_RAM[23:16], Data_RAM[31:24]}), .sel(sw));  // open: en
  Bit_Extender #(.in_width(32), .out_width(7)) bit_extender_1 (.in(A), .out(TTY_Data));
  ALU_2 alu_1 (
    .in_1(A), .in_2(B), .in_3(Op_code), .in_4(Func_code), .in_5(Cst), .in_6(I), .Output(ALU_R), .Hi(Hi_in),
    .Lo(Lo_in), .LHiLo(LHiLo));

  // Other names for the same wires on the sheet: CLK = in_3; Flag_KBD = in_7; Func[5:0] = Func_code; InstEN = in_6;
  //   Instruction[31:0] = in_1; KBD_Data[31:0] = in_2; Mem_Adrs[31:0] = Memory_Address; Op[5:0] = Op_code;
  //   PCen = in_5; R_W = in_9; RST = in_4; SPen = in_10; startEN = in_8
endmodule

module Memory_Address (
  input  [31:0] in_1,
  input  [31:0] in_2,
  input  [31:0] in_3,
  input  in_4,
  input  in_5,
  output [31:0] Memory_Address
);

  wire [31:0] multiplexer_1_out;

  Multiplexer #(.width(32)) multiplexer_1 (.in0(in_1), .in1(in_2), .out(multiplexer_1_out), .sel(in_4));  // open: en
  Multiplexer #(.width(32)) multiplexer_2 (
    .in0(multiplexer_1_out), .in1(in_3), .out(Memory_Address), .sel(in_5));  // open: en

  // Other names for the same wires on the sheet: ALU[31:0] = in_3; PC[31:0] = in_1; SP[31:0] = in_2; SP_flag = in_4;
  //   Word_flag = in_5
endmodule

module Operations_on_Registers_Decoder (
  input  [5:0] in_1,
  input  [5:0] in_2,
  output mfhi,
  output mflo,
  output pop,
  output push,
  output lw,
  output sw,
  output tty,
  output rnd,
  output kbd,
  output halt
);

  wire comparator_1_eq, comparator_2_eq, comparator_3_eq, comparator_4_eq, comparator_5_eq, comparator_6_eq,
       comparator_9_eq, comparator_10_eq, comparator_11_eq, comparator_12_eq, comparator_13_eq;

  Comparator_part #(.width(6)) comparator_1 (.a(in_1), .b({6{1'b0}}), .eq(comparator_1_eq));  // open: gt, lt
  and and_1 (mflo, comparator_1_eq, comparator_2_eq);
  Comparator_part #(.width(6)) comparator_2 (.a(in_2), .b(6'b010010), .eq(comparator_2_eq));  // open: gt, lt
  and and_2 (mfhi, comparator_1_eq, comparator_3_eq);
  Comparator_part #(.width(6)) comparator_3 (.a(in_2), .b(6'b010000), .eq(comparator_3_eq));  // open: gt, lt
  Comparator_part #(.width(6)) comparator_4 (.a(in_1), .b(6'b111000), .eq(comparator_4_eq));  // open: gt, lt
  and and_3 (pop, comparator_4_eq, comparator_5_eq);
  Comparator_part #(.width(6)) comparator_5 (.a(in_2), .b({6{1'b0}}), .eq(comparator_5_eq));  // open: gt, lt
  and and_4 (push, comparator_4_eq, comparator_6_eq);
  Comparator_part #(.width(6)) comparator_6 (.a(in_2), .b(6'b000001), .eq(comparator_6_eq));  // open: gt, lt
  Comparator_part #(.width(6)) comparator_7 (.a(in_1), .b(6'b100011), .eq(lw));  // open: gt, lt
  Comparator_part #(.width(6)) comparator_8 (.a(in_1), .b(6'b101011), .eq(sw));  // open: gt, lt
  Comparator_part #(.width(6)) comparator_9 (.a(in_1), .b({6{1'b1}}), .eq(comparator_9_eq));  // open: gt, lt
  and and_5 (tty, comparator_9_eq, comparator_10_eq);
  Comparator_part #(.width(6)) comparator_10 (.a(in_2), .b(6'b000001), .eq(comparator_10_eq));  // open: gt, lt
  and and_6 (rnd, comparator_9_eq, comparator_11_eq);
  Comparator_part #(.width(6)) comparator_11 (.a(in_2), .b(6'b000010), .eq(comparator_11_eq));  // open: gt, lt
  and and_7 (kbd, comparator_9_eq, comparator_12_eq);
  Comparator_part #(.width(6)) comparator_12 (.a(in_2), .b(6'b000100), .eq(comparator_12_eq));  // open: gt, lt
  and and_8 (halt, comparator_9_eq, comparator_13_eq);
  Comparator_part #(.width(6)) comparator_13 (.a(in_2), .b({6{1'b1}}), .eq(comparator_13_eq));  // open: gt, lt

  // Other names for the same wires on the sheet: Func_code[5:0] = in_2; Op_code[5:0] = in_1
endmodule

module Operation_code (
  input  [5:0] in_1,
  output R,
  output I,
  output J
);

  wire comparator_2_eq, comparator_3_eq, comparator_4_eq;

  Comparator_part #(.width(6)) comparator_1 (.a(in_1), .b(6'b000010), .eq(J));  // open: gt, lt
  Comparator_part #(.width(6)) comparator_2 (.a(in_1), .b({6{1'b0}}), .eq(comparator_2_eq));  // open: gt, lt
  Comparator_part #(.width(6)) comparator_3 (.a(in_1), .b(6'b111000), .eq(comparator_3_eq));  // open: gt, lt
  or or_1 (R, comparator_2_eq, comparator_3_eq, comparator_4_eq);
  Comparator_part #(.width(6)) comparator_4 (.a(in_1), .b({6{1'b1}}), .eq(comparator_4_eq));  // open: gt, lt
  and and_1 (I, ~R, ~J);  // AND_Gate

  // Other names for the same wires on the sheet: Op_code[5:0] = in_1
endmodule

module ALU_2 (
  input  [31:0] in_1,
  input  [31:0] in_2,
  input  [5:0] in_3,
  input  [5:0] in_4,
  input  [15:0] in_5,
  input  in_6,
  output [31:0] Output,
  output [31:0] Hi,
  output [31:0] Lo,
  output LHiLo
);

  wire Sign;
  wire [3:0] Selector;
  wire [31:0] ConstanteB, multiplexer_1_out;

  Multiplexer #(.width(32)) multiplexer_1 (
    .in0(in_2), .in1(ConstanteB), .out(multiplexer_1_out), .sel(in_6));  // open: en
  ALU_Control alu_control_1 (
    .in_1(in_3), .in_2(in_4), .in_3(in_5), .Selector(Selector), .Sign(Sign), .Constante(ConstanteB),
    .LHiLo(LHiLo));
  ALU_Operations alu_operations_1 (
    .in_1(in_1), .in_2(multiplexer_1_out), .in_3(Selector), .in_4(Sign), .Output(Output), .Hi(Hi), .Lo(Lo));

  // Other names for the same wires on the sheet: A[31:0] = in_1; B[31:0] = in_2; Constante[15:0] = in_5;
  //   Func_code[5:0] = in_4; Op_code[5:0] = in_3; Type_I = in_6
endmodule

module ALU_Operations (
  input  [31:0] in_1,
  input  [31:0] in_2,
  input  [3:0] in_3,
  input  in_4,
  output [31:0] Output,
  output [31:0] Hi,
  output [31:0] Lo
);

  wire flag_mul;
  wire [31:0] add, \and , div_Q, div_R, mul_Hi, mul_Lo, \nor , \or , slt___sltu, sub, \xor ;

  assign \and  = in_1 & in_2;  // AND_Gate and_1, 32 bits wide
  assign \or  = in_1 | in_2;  // OR_Gate or_1, 32 bits wide
  assign \nor  = ~(in_1 | in_2);  // NOR_Gate nor_1, 32 bits wide
  assign \xor  = in_1 ^ in_2;  // XOR_Gate xor_1, 32 bits wide
  Adder #(.width(32)) adder_1 (.a(in_1), .b(in_2), .out(add));  // open: cin, cout
  Subtractor #(.width(32)) subtractor_1 (.a(in_1), .b(in_2), .out(sub));  // open: bin, bout
  Multiplier_C2 multiplier_c2_1 (.in_1(in_1), .in_2(in_2), .in_3(in_4), .Hi(mul_Hi), .Lo(mul_Lo));
  Divider divider_1 (.in_1(in_1), .in_2(in_2), .in_3(in_4), .Quotient(div_Q), .Remainder(div_R));
  Comparator comparator_1 (.in_1(in_1), .in_2(in_2), .in_3(in_4), .Output(slt___sltu));
  Comparator_part #(.width(4)) comparator_2 (.a(in_3), .b(4'b0010), .eq(flag_mul));  // open: gt, lt
  Multiplexer #(.select(4), .width(32)) multiplexer_1 (
    .in0(add), .in1(sub), .in4(\and ), .in5(\or ), .in6(\nor ), .in7(\xor ), .in8(slt___sltu), .out(Output),
    .sel(in_3));  // open: in2, in3, in9, in10, in11, in12, in13, in14, in15, en
  Multiplexer #(.width(32)) multiplexer_2 (.in0(div_R), .in1(mul_Hi), .out(Hi), .sel(flag_mul));  // open: en
  Multiplexer #(.width(32)) multiplexer_3 (.in0(div_Q), .in1(mul_Lo), .out(Lo), .sel(flag_mul));  // open: en

  // Other names for the same wires on the sheet: A[31:0] = in_1; B[31:0] = in_2; Op[3:0] = in_3; sign = in_4

  // Notes on the sheet:
  //   Logic
  //   Arithmetic
  //   Comparison
endmodule

module ALU_Control (
  input  [5:0] in_1,
  input  [5:0] in_2,
  input  [15:0] in_3,
  output [3:0] Selector,
  output Sign,
  output [31:0] Constante,
  output LHiLo
);

  wire add, addi, \and , and_13_out, andi, comparator_1_eq, comparator_2_eq, comparator_3_eq,
       comparator_4_eq, comparator_5_eq, comparator_6_eq, comparator_7_eq, comparator_8_eq, comparator_9_eq,
       comparator_10_eq, comparator_11_eq, comparator_12_eq, comparator_13_eq, div, divu, mult, mulu, \nor ,
       \or , ori, slt, slti, sltiu, sltu, sub, \xor , xori;

  Comparator_part #(.width(6)) comparator_1 (.a(in_1), .b({6{1'b0}}), .eq(comparator_1_eq));  // open: gt, lt
  Comparator_part #(.width(6)) comparator_2 (.a(in_2), .b(6'b100000), .eq(comparator_2_eq));  // open: gt, lt
  Comparator_part #(.width(6)) comparator_3 (.a(in_2), .b(6'b100010), .eq(comparator_3_eq));  // open: gt, lt
  Comparator_part #(.width(6)) comparator_4 (.a(in_2), .b(6'b011000), .eq(comparator_4_eq));  // open: gt, lt
  Comparator_part #(.width(6)) comparator_5 (.a(in_2), .b(6'b011001), .eq(comparator_5_eq));  // open: gt, lt
  Comparator_part #(.width(6)) comparator_6 (.a(in_2), .b(6'b011010), .eq(comparator_6_eq));  // open: gt, lt
  Comparator_part #(.width(6)) comparator_7 (.a(in_2), .b(6'b011011), .eq(comparator_7_eq));  // open: gt, lt
  Comparator_part #(.width(6)) comparator_8 (.a(in_2), .b(6'b100100), .eq(comparator_8_eq));  // open: gt, lt
  Comparator_part #(.width(6)) comparator_9 (.a(in_2), .b(6'b100101), .eq(comparator_9_eq));  // open: gt, lt
  Comparator_part #(.width(6)) comparator_10 (.a(in_2), .b(6'b100111), .eq(comparator_10_eq));  // open: gt, lt
  Comparator_part #(.width(6)) comparator_11 (.a(in_2), .b(6'b101000), .eq(comparator_11_eq));  // open: gt, lt
  Comparator_part #(.width(6)) comparator_12 (.a(in_2), .b(6'b101010), .eq(comparator_12_eq));  // open: gt, lt
  Comparator_part #(.width(6)) comparator_13 (.a(in_2), .b(6'b101011), .eq(comparator_13_eq));  // open: gt, lt
  and and_1 (add, comparator_1_eq, comparator_2_eq);
  and and_2 (sub, comparator_1_eq, comparator_3_eq);
  and and_3 (mult, comparator_1_eq, comparator_4_eq);
  and and_4 (mulu, comparator_1_eq, comparator_5_eq);
  and and_5 (div, comparator_1_eq, comparator_6_eq);
  and and_6 (divu, comparator_1_eq, comparator_7_eq);
  and and_7 (\and , comparator_1_eq, comparator_8_eq);
  and and_8 (\or , comparator_1_eq, comparator_9_eq);
  and and_9 (\nor , comparator_1_eq, comparator_10_eq);
  and and_10 (\xor , comparator_1_eq, comparator_11_eq);
  and and_11 (slt, comparator_1_eq, comparator_12_eq);
  and and_12 (sltu, comparator_1_eq, comparator_13_eq);
  Comparator_part #(.width(6)) comparator_14 (.a(in_1), .b(6'b001000), .eq(addi));  // open: gt, lt
  Comparator_part #(.width(6)) comparator_15 (.a(in_1), .b(6'b001100), .eq(andi));  // open: gt, lt
  Comparator_part #(.width(6)) comparator_16 (.a(in_1), .b(6'b001101), .eq(ori));  // open: gt, lt
  Comparator_part #(.width(6)) comparator_17 (.a(in_1), .b(6'b001110), .eq(xori));  // open: gt, lt
  Comparator_part #(.width(6)) comparator_18 (.a(in_1), .b(6'b001010), .eq(slti));  // open: gt, lt
  Comparator_part #(.width(6)) comparator_19 (.a(in_1), .b(6'b001011), .eq(sltiu));  // open: gt, lt
  or or_1 (Selector[0], ori, \or , div, sub, divu, \xor , xori);
  or or_2 (Selector[1], \xor , divu, mulu, mult, div, \nor , xori);
  or or_3 (Selector[2], ori, \xor , \or , \and , \nor , andi, xori);
  or or_4 (Selector[3], slti, slt, sltu, sltiu);
  and and_13 (and_13_out, in_3[15], ~andi, ~ori, ~xori);  // AND_Gate
  or or_5 (Sign, mult, div, slt, slti);
  assign Constante[31:15] = {{16{and_13_out}}, and_13_out};  // Bit_Extender bit_extender_1
  or or_6 (LHiLo, mult, mulu, divu, div);

  assign Constante[14:0] = in_3[14:0];

  // Other names for the same wires on the sheet: Constante_t[15:0] = in_3; Func_code[5:0] = in_2; Op_code[5:0] = in_1

  // Notes on the sheet:
  //   Type R
  //   Type I
endmodule

module Multiplier (
  input  [31:0] in_1,
  input  [31:0] in_2,
  input  in_3,
  output [31:0] Hi,
  output [31:0] Lo
);

  wire a1, adder_1_cout, adder_5_cout, adder_7_cout, and_4_out, and_5_out, Aux1, b1, shifter_7_out;
  wire [31:0] a31, adder_1_out, adder_2_out, adder_3_out, adder_5_out, adder_6_out, and_1_out, and_2_out,
       AuxF1, AuxF2, AuxHi, AuxHi2, AuxHiF, AuxLo, AuxLoF, b31, bit_extender_3_out, bit_extender_6_out,
       bit_extender_7_out, bit_extender_8_out, F1, F2, Hi_t, HiU, Lo_t, LoU, shifter_1_out, shifter_2_out;

  Shifter #(.width(32)) shifter_1 (.in(a31), .\dist (5'b00001), .out(shifter_1_out));
  Shifter #(.width(32)) shifter_2 (.in(b31), .\dist (5'b00001), .out(shifter_2_out));
  Multiplexer #(.width(32)) multiplexer_1 (.in0({32{1'b0}}), .in1(shifter_1_out), .out(AuxF1), .sel(b1));  // open: en
  Shifter #(.width(32), .shift("lr")) shifter_3 (.in(in_1), .\dist (5'b00001), .out(a31));
  assign and_1_out = in_1 & 32'h1;  // AND_Gate and_1, 32 bits wide
  Multiplexer #(.width(32)) multiplexer_2 (.in0({32{1'b0}}), .in1(shifter_2_out), .out(AuxF2), .sel(a1));  // open: en
  Bit_Extender #(.in_width(32), .out_width(1)) bit_extender_1 (.in(and_1_out), .out(a1));
  Multiplier_part #(.width(32)) multiplier_1 (.a(a31), .b(b31), .out(AuxLo), .cout(AuxHi));  // open: cin
  Shifter #(.width(32)) shifter_4 (.in(AuxLo), .\dist (5'b00010), .out(AuxLoF));
  Shifter #(.width(32), .shift("lr")) shifter_5 (.in(in_2), .\dist (5'b00001), .out(b31));
  assign and_2_out = in_2 & 32'h1;  // AND_Gate and_2, 32 bits wide
  and and_3 (Aux1, a1, b1);
  Bit_Extender #(.in_width(32), .out_width(1)) bit_extender_2 (.in(and_2_out), .out(b1));
  Adder #(.width(32)) adder_1 (.a(AuxLoF), .b(AuxF1), .out(adder_1_out), .cout(adder_1_cout));  // open: cin
  assign bit_extender_3_out = {{31{1'b0}}, adder_1_cout};  // Bit_Extender bit_extender_3
  Shifter #(.width(32)) shifter_6 (.in(AuxHi), .\dist (5'b00010), .out(AuxHi2));
  and and_4 (and_4_out, AuxLo[30], 1'b1);
  and and_5 (and_5_out, AuxLo[31], 1'b1);
  Adder #(.width(32)) adder_2 (.a(AuxHi2), .b(F1), .out(adder_2_out));  // open: cin, cout
  Adder #(.width(32)) adder_3 (.a(bit_extender_3_out), .b(AuxHiF), .out(adder_3_out));  // open: cin, cout
  assign F2 = {{31{1'b0}}, and_4_out};  // Bit_Extender bit_extender_4
  Shifter #(.width(1)) shifter_7 (.in(and_5_out), .\dist (1'b1), .out(shifter_7_out));
  assign F1 = {{31{1'b0}}, shifter_7_out};  // Bit_Extender bit_extender_5
  Adder #(.width(32)) adder_4 (.a(adder_2_out), .b(F2), .out(AuxHiF));  // open: cin, cout
  Adder #(.width(32)) adder_5 (.a(adder_1_out), .b(AuxF2), .out(adder_5_out), .cout(adder_5_cout));  // open: cin
  assign bit_extender_6_out = {{31{1'b0}}, adder_5_cout};  // Bit_Extender bit_extender_6
  assign bit_extender_7_out = {{31{1'b0}}, Aux1};  // Bit_Extender bit_extender_7
  Adder #(.width(32)) adder_6 (.a(bit_extender_6_out), .b(adder_3_out), .out(adder_6_out));  // open: cin, cout
  Adder #(.width(32)) adder_7 (.a(adder_5_out), .b(bit_extender_7_out), .out(LoU), .cout(adder_7_cout));  // open: cin
  Multiplexer #(.width(32)) multiplexer_3 (.in0(HiU), .in1(Hi_t), .out(Hi), .sel(in_3));  // open: en
  Multiplexer #(.width(32)) multiplexer_4 (.in0(LoU), .in1(Lo_t), .out(Lo), .sel(in_3));  // open: en
  assign bit_extender_8_out = {{31{1'b0}}, adder_7_cout};  // Bit_Extender bit_extender_8
  Adder #(.width(32)) adder_8 (.a(bit_extender_8_out), .b(adder_6_out), .out(HiU));  // open: cin, cout
  Multiplier_part #(.width(32)) multiplier_2 (.a(in_1), .b(in_2), .out(Lo_t), .cout(Hi_t));  // open: cin

  // Other names for the same wires on the sheet: A[31:0] = in_1; B[31:0] = in_2; sign = in_3

  // Notes on the sheet:
  //   AuxF1 = a31*b1*2
  //   AuxF2 = a1*b31*2
  //   A = a31*2+a1      B = b31*2+b1
  //   {AuxHiF,AuxLoF} = a31*b31*4
  //   Aux1 = a1*b1
  //   {HiU,LoU} = {AuxHiF,AuxLoF}+AuxF1+AuxF2+Aux1
endmodule

module Multiplier_C2 (
  input  [31:0] in_1,
  input  [31:0] in_2,
  input  in_3,
  output [31:0] Hi,
  output [31:0] Lo
);

  wire negA, negB;
  wire [31:0] Hi_t, HiU, Lo_t, LoU, multiplexer_1_out, multiplexer_2_out, negator_1_out, negator_2_out;

  Negator #(.width(32)) negator_1 (.in(in_1), .out(negator_1_out));
  Negator #(.width(32)) negator_2 (.in(in_2), .out(negator_2_out));
  Comparator_part #(.width(32)) comparator_1 (.a(in_1), .b({32{1'b0}}), .lt(negA));  // open: gt, eq
  Multiplexer #(.width(32)) multiplexer_1 (
    .in0(in_1), .in1(negator_1_out), .out(multiplexer_1_out), .sel(negA));  // open: en
  Multiplexer #(.width(32)) multiplexer_2 (
    .in0(in_2), .in1(negator_2_out), .out(multiplexer_2_out), .sel(negB));  // open: en
  Multiplier_part #(.width(32)) multiplier_1 (
    .a(multiplexer_1_out), .b(multiplexer_2_out), .out(LoU), .cout(HiU));  // open: cin
  Comparator_part #(.width(32)) comparator_2 (.a(in_2), .b({32{1'b0}}), .lt(negB));  // open: gt, eq
  Multiplier_part #(.width(32)) multiplier_2 (.a(in_1), .b(in_2), .out(Lo_t), .cout(Hi_t));  // open: cin
  Multiplexer #(.width(32)) multiplexer_3 (.in0(HiU), .in1(Hi_t), .out(Hi), .sel(in_3));  // open: en
  Multiplexer #(.width(32)) multiplexer_4 (.in0(LoU), .in1(Lo_t), .out(Lo), .sel(in_3));  // open: en

  // Other names for the same wires on the sheet: A[31:0] = in_1; B[31:0] = in_2; sign = in_3
endmodule

module Divider (
  input  [31:0] in_1,
  input  [31:0] in_2,
  input  in_3,
  output [31:0] Quotient,
  output [31:0] Remainder
);

  wire is_neg_A, is_neg_B, is_neg_quotient;
  wire [31:0] abs_A, abs_B, adder_1_out, aux_rem, divider_1_out, multiplexer_2_out, negator_1_out,
       negator_2_out, negator_3_out, subtractor_1_out;

  Negator #(.width(32)) negator_1 (.in(in_1), .out(negator_1_out));
  and and_1 (is_neg_A, in_1[31], in_3);
  Multiplexer #(.width(32)) multiplexer_1 (.in0(in_1), .in1(negator_1_out), .out(abs_A), .sel(is_neg_A));  // open: en
  Divider_part #(.width(32)) divider_1 (.a(abs_A), .b(abs_B), .out(divider_1_out), .rem(aux_rem));  // open: upper
  xor xor_1 (is_neg_quotient, is_neg_A, is_neg_B);
  Multiplexer #(.width(32)) multiplexer_2 (
    .in0(divider_1_out), .in1(adder_1_out), .out(multiplexer_2_out), .sel(is_neg_A));  // open: en
  Adder #(.width(32)) adder_1 (.a(divider_1_out), .b(32'h1), .out(adder_1_out));  // open: cin, cout
  Subtractor #(.width(32)) subtractor_1 (.a(abs_B), .b(aux_rem), .out(subtractor_1_out));  // open: bin, bout
  Negator #(.width(32)) negator_2 (.in(in_2), .out(negator_2_out));
  Negator #(.width(32)) negator_3 (.in(multiplexer_2_out), .out(negator_3_out));
  Multiplexer #(.width(32)) multiplexer_3 (
    .in0(aux_rem), .in1(subtractor_1_out), .out(Remainder), .sel(is_neg_A));  // open: en
  and and_2 (is_neg_B, in_2[31], in_3);
  Multiplexer #(.width(32)) multiplexer_4 (.in0(in_2), .in1(negator_2_out), .out(abs_B), .sel(is_neg_B));  // open: en
  Multiplexer #(.width(32)) multiplexer_5 (
    .in0(multiplexer_2_out), .in1(negator_3_out), .out(Quotient), .sel(is_neg_quotient));  // open: en

  // Other names for the same wires on the sheet: A[31:0] = in_1; B[31:0] = in_2; sign = in_3
endmodule

module Comparator (
  input  [31:0] in_1,
  input  [31:0] in_2,
  input  in_3,
  output [31:0] Output
);

  wire multiplexer_1_out, slt, sltu;

  Comparator_part #(.width(32)) comparator_1 (.a(in_1), .b(in_2), .lt(slt));  // open: gt, eq
  Comparator_part #(.width(32), .mode("unsigned")) comparator_2 (.a(in_1), .b(in_2), .lt(sltu));  // open: gt, eq
  Multiplexer multiplexer_1 (.in0(sltu), .in1(slt), .out(multiplexer_1_out), .sel(in_3));  // open: en
  assign Output = {{31{1'b0}}, multiplexer_1_out};  // Bit_Extender bit_extender_1

  // Other names for the same wires on the sheet: A[31:0] = in_1; B[31:0] = in_2; sign = in_3
endmodule

module Register_File (
  input  [31:0] in_1,
  input  [4:0] in_2,
  input  [4:0] in_3,
  input  [4:0] in_4,
  input  [31:0] in_5,
  input  [31:0] in_6,
  input  in_7,
  input  in_8,
  input  in_9,
  input  in_10,
  input  in_11,
  input  in_12,
  input  in_13,
  input  in_14,
  input  in_15,
  input  in_16,
  output [31:0] A,
  output [31:0] B,
  output [31:0] Hi,
  output [31:0] Lo,
  output [31:0] SP
);

  wire en31, L0, L1, L2, L3, L4, L5, L6, L7, L8, L9, L10, L11, L12, L13, L14, L15, L16, L17, L18, L19, L20,
       L21, L22, L23, L24, L25, L26, L27, L28, L29, L30, L31;
  wire [1:0] selector;
  wire [31:0] adder_1_out, D31, DI, multiplexer_1_out, Q0, Q1, Q2, Q3, Q4, Q5, Q6, Q7, Q8, Q9, Q10, Q11, Q12,
       Q13, Q14, Q15, Q16, Q17, Q18, Q19, Q20, Q21, Q22, Q23, Q24, Q25, Q26, Q27, Q28, Q29, Q30, RND, SP_t;

  Register #(.width(32)) register_1 (.D({32{1'b0}}), .en(L0), .Q(Q0), .clk(in_14), .clr(in_15));
  Register #(.width(32)) register_2 (.D(DI), .en(L8), .Q(Q8), .clk(in_14), .clr(in_15));
  Register #(.width(32)) register_3 (.D(DI), .en(L16), .Q(Q16), .clk(in_14), .clr(in_15));
  Register #(.width(32)) register_4 (.D(DI), .en(L24), .Q(Q24), .clk(in_14), .clr(in_15));
  Random #(.width(32), .seed(7)) random_1 (.clk(in_14), .out(RND));  // open: next, clr
  Demultiplexer #(.select(5)) demultiplexer_1 (
    .out0(L0), .out1(L1), .out2(L2), .out3(L3), .out4(L4), .out5(L5), .out6(L6), .out7(L7), .out8(L8),
    .out9(L9), .out10(L10), .out11(L11), .out12(L12), .out13(L13), .out14(L14), .out15(L15), .out16(L16),
    .out17(L17), .out18(L18), .out19(L19), .out20(L20), .out21(L21), .out22(L22), .out23(L23), .out24(L24),
    .out25(L25), .out26(L26), .out27(L27), .out28(L28), .out29(L29), .out30(L30), .out31(L31), .in(in_7),
    .sel(in_2));  // open: en
  Register #(.width(32)) register_5 (.D(DI), .en(L1), .Q(Q1), .clk(in_14), .clr(in_15));
  Register #(.width(32)) register_6 (.D(DI), .en(L9), .Q(Q9), .clk(in_14), .clr(in_15));
  Register #(.width(32)) register_7 (.D(DI), .en(L17), .Q(Q17), .clk(in_14), .clr(in_15));
  Register #(.width(32)) register_8 (.D(DI), .en(L25), .Q(Q25), .clk(in_14), .clr(in_15));
  Multiplexer #(.width(32)) multiplexer_1 (
    .in0(32'h4), .in1(32'hfffffffc), .out(multiplexer_1_out), .sel(in_10));  // open: en
  Register #(.width(32)) register_9 (.D(DI), .en(L2), .Q(Q2), .clk(in_14), .clr(in_15));
  Register #(.width(32)) register_10 (.D(DI), .en(L10), .Q(Q10), .clk(in_14), .clr(in_15));
  Register #(.width(32)) register_11 (.D(DI), .en(L18), .Q(Q18), .clk(in_14), .clr(in_15));
  Register #(.width(32)) register_12 (.D(DI), .en(L26), .Q(Q26), .clk(in_14), .clr(in_15));
  Adder #(.width(32)) adder_1 (.a(multiplexer_1_out), .b(SP), .out(adder_1_out));  // open: cin, cout
  or or_1 (selector[0], in_12, in_8);
  or or_2 (selector[1], in_9, in_12);
  Multiplexer #(.width(32)) multiplexer_2 (.in0(adder_1_out), .in1({32{1'b1}}), .out(SP_t), .sel(in_15));  // open: en
  Register #(.width(32)) register_13 (.D(DI), .en(L3), .Q(Q3), .clk(in_14), .clr(in_15));
  Register #(.width(32)) register_14 (.D(DI), .en(L11), .Q(Q11), .clk(in_14), .clr(in_15));
  Register #(.width(32)) register_15 (.D(DI), .en(L19), .Q(Q19), .clk(in_14), .clr(in_15));
  Register #(.width(32)) register_16 (.D(DI), .en(L27), .Q(Q27), .clk(in_14), .clr(in_15));
  Multiplexer #(.width(32)) multiplexer_3 (.in0(SP_t), .in1(DI), .out(D31), .sel(L31));  // open: en
  Multiplexer #(.select(5), .width(32)) multiplexer_4 (
    .in0(Q0), .in1(Q1), .in2(Q2), .in3(Q3), .in4(Q4), .in5(Q5), .in6(Q6), .in7(Q7), .in8(Q8), .in9(Q9),
    .in10(Q10), .in11(Q11), .in12(Q12), .in13(Q13), .in14(Q14), .in15(Q15), .in16(Q16), .in17(Q17),
    .in18(Q18), .in19(Q19), .in20(Q20), .in21(Q21), .in22(Q22), .in23(Q23), .in24(Q24), .in25(Q25),
    .in26(Q26), .in27(Q27), .in28(Q28), .in29(Q29), .in30(Q30), .in31(SP), .out(A), .sel(in_3));  // open: en
  Register #(.width(32)) register_17 (.D(DI), .en(L4), .Q(Q4), .clk(in_14), .clr(in_15));
  Register #(.width(32)) register_18 (.D(DI), .en(L12), .Q(Q12), .clk(in_14), .clr(in_15));
  Register #(.width(32)) register_19 (.D(DI), .en(L20), .Q(Q20), .clk(in_14), .clr(in_15));
  Register #(.width(32)) register_20 (.D(DI), .en(L28), .Q(Q28), .clk(in_14), .clr(in_15));
  Multiplexer #(.select(5), .width(32)) multiplexer_5 (
    .in0(Q0), .in1(Q1), .in2(Q2), .in3(Q3), .in4(Q4), .in5(Q5), .in6(Q6), .in7(Q7), .in8(Q8), .in9(Q9),
    .in10(Q10), .in11(Q11), .in12(Q12), .in13(Q13), .in14(Q14), .in15(Q15), .in16(Q16), .in17(Q17),
    .in18(Q18), .in19(Q19), .in20(Q20), .in21(Q21), .in22(Q22), .in23(Q23), .in24(Q24), .in25(Q25),
    .in26(Q26), .in27(Q27), .in28(Q28), .in29(Q29), .in30(Q30), .in31(SP), .out(B), .sel(in_4));  // open: en
  Multiplexer #(.select(2), .width(32)) multiplexer_6 (
    .in0(in_1), .in1(Hi), .in2(Lo), .in3(RND), .out(DI), .sel(selector));  // open: en
  or or_3 (en31, L31, in_10, in_16, in_11, in_15);
  Register #(.width(32)) register_21 (.D(DI), .en(L5), .Q(Q5), .clk(in_14), .clr(in_15));
  Register #(.width(32)) register_22 (.D(DI), .en(L13), .Q(Q13), .clk(in_14), .clr(in_15));
  Register #(.width(32)) register_23 (.D(DI), .en(L21), .Q(Q21), .clk(in_14), .clr(in_15));
  Register #(.width(32)) register_24 (.D(DI), .en(L29), .Q(Q29), .clk(in_14), .clr(in_15));
  Register #(.width(32)) register_25 (.D(in_5), .en(in_13), .Q(Hi), .clk(in_14), .clr(in_15));
  Register #(.width(32)) register_26 (.D(in_6), .en(in_13), .Q(Lo), .clk(in_14), .clr(in_15));
  Register #(.width(32)) register_27 (.D(DI), .en(L6), .Q(Q6), .clk(in_14), .clr(in_15));
  Register #(.width(32)) register_28 (.D(DI), .en(L14), .Q(Q14), .clk(in_14), .clr(in_15));
  Register #(.width(32)) register_29 (.D(DI), .en(L22), .Q(Q22), .clk(in_14), .clr(in_15));
  Register #(.width(32)) register_30 (.D(DI), .en(L30), .Q(Q30), .clk(in_14), .clr(in_15));
  Register #(.width(32)) register_31 (.D(DI), .en(L7), .Q(Q7), .clk(in_14), .clr(in_15));
  Register #(.width(32)) register_32 (.D(DI), .en(L15), .Q(Q15), .clk(in_14), .clr(in_15));
  Register #(.width(32)) register_33 (.D(DI), .en(L23), .Q(Q23), .clk(in_14), .clr(in_15));
  Register #(.width(32)) register_34 (.D(D31), .en(en31), .Q(SP), .clk(in_14));  // open: clr

  // Other names for the same wires on the sheet: clock = in_14; DA[4:0] = in_2; DataIn[31:0] = in_1;
  //   Hi_t[31:0] = in_5; LHiLo = in_13; Lo_t[31:0] = in_6; mfhi = in_8; mflo = in_9; pop = in_11; push = in_10;
  //   Q31[31:0] = SP; QHi[31:0] = Hi; QLo[31:0] = Lo; R_W = in_7; reset = in_15; rnd_t = in_12; SA[4:0] = in_3;
  //   SB[4:0] = in_4; SPen = in_16
endmodule

module Program_Counter (
  input  [31:0] PC_star,
  input  in_2,
  input  in_3,
  input  in_4,
  output [31:0] PC
);

  Register #(.width(32)) register_1 (.D(PC_star), .en(in_4), .Q(PC), .clk(in_2), .clr(in_3));

  // Other names for the same wires on the sheet: CLK = in_2; EN = in_4; RST = in_3
endmodule

module Instruction_Decoder (
  input  [31:0] Instruction,
  input  in_2,
  input  in_3,
  input  in_4,
  output [5:0] Op_code,
  output [4:0] Rs,
  output [4:0] Rt,
  output [4:0] Rd,
  output [5:0] Func_code,
  output [15:0] Constante,
  output [25:0] Destino_Salto
);

  Register #(.width(32)) register_1 (
    .D(Instruction), .en(in_2), .Q({Op_code, Destino_Salto[25:16], Constante}), .clk(in_3), .clr(in_4));

  assign Destino_Salto[15:0] = Constante;
  assign Func_code = Constante[5:0];
  assign Rd = Constante[15:11];
  assign Rs = Destino_Salto[25:21];
  assign Rt = Destino_Salto[20:16];

  // Other names for the same wires on the sheet: CLK = in_3; en = in_2; RST = in_4
endmodule

module Branch_Control (
  input  [31:0] in_1,
  input  [31:0] in_2,
  input  [31:0] in_3,
  input  [15:0] in_4,
  input  [25:0] in_5,
  input  [5:0] in_6,
  input  [5:0] in_7,
  output [31:0] Next_Instruction_Address
);

  wire and_1_out, and_2_out, and_3_out, and_4_out, and_5_out, beq, bgtz, blez, bltz, bne, comparator_1_eq,
       comparator_1_gt, comparator_1_lt, comparator_2_eq, Cond, j, jr, or_1_out;
  wire [31:0] adder_1_out, adder_2_out, multiplexer_1_out, multiplexer_2_out;
  wire [31:17] Offset32;

  assign Offset32 = {{14{in_4[15]}}, in_4[15]};  // Bit_Extender bit_extender_1
  Jump_Type jump_type_1 (
    .in_1(in_6), .in_2(in_7), .beq(beq), .bne(bne), .blez(blez), .bgtz(bgtz), .bltz(bltz), .j(j), .jr(jr));
  Multiplexer #(.width(32)) multiplexer_1 (
    .in0({32{1'b0}}), .in1({Offset32, in_4[14:0], 2'b00}), .out(multiplexer_1_out), .sel(Cond));  // open: en
  Adder #(.width(32)) adder_1 (.a(in_1), .b(32'h4), .out(adder_1_out));  // open: cin, cout
  Adder #(.width(32)) adder_2 (.a(multiplexer_1_out), .b(adder_1_out), .out(adder_2_out));  // open: cin, cout
  Comparator_part #(.width(32)) comparator_1 (
    .a(in_2), .b({32{1'b0}}), .gt(comparator_1_gt), .eq(comparator_1_eq), .lt(comparator_1_lt));
  Multiplexer #(.width(32)) multiplexer_2 (
    .in0(adder_2_out), .in1({in_1[31:28], in_5, 2'b00}), .out(multiplexer_2_out), .sel(j));  // open: en
  Comparator_part #(.width(32)) comparator_2 (.a(in_2), .b(in_3), .eq(comparator_2_eq));  // open: gt, lt
  or or_1 (or_1_out, comparator_1_eq, comparator_1_lt);
  Multiplexer #(.width(32)) multiplexer_3 (
    .in0(multiplexer_2_out), .in1(in_2), .out(Next_Instruction_Address), .sel(jr));  // open: en
  and and_1 (and_1_out, beq, comparator_2_eq);
  and and_2 (and_2_out, bne, ~comparator_2_eq);  // AND_Gate
  and and_3 (and_3_out, bgtz, comparator_1_gt);
  and and_4 (and_4_out, blez, or_1_out);
  and and_5 (and_5_out, bltz, comparator_1_lt);
  or or_2 (Cond, and_1_out, and_2_out, and_3_out, and_4_out, and_5_out);

  // Other names for the same wires on the sheet: Destine[25:0] = in_5; Destine32[31:2] = {in_1[31:28], in_5};
  //   PC[31:0] = in_1; Func_code[5:0] = in_7; Offset[15:0] = in_4; Offset32[16:2] = in_4[14:0]; Op_code[5:0] = in_6;
  //   PC_star[31:0] = Next_Instruction_Address; Rs[31:0] = in_2; Rt[31:0] = in_3
endmodule

module Jump_Type (
  input  [5:0] in_1,
  input  [5:0] in_2,
  output beq,
  output bne,
  output blez,
  output bgtz,
  output bltz,
  output j,
  output jr
);

  wire comparator_7_eq, comparator_8_eq;

  Comparator_part #(.width(6)) comparator_1 (.a(in_1), .b(6'b000100), .eq(beq));  // open: gt, lt
  Comparator_part #(.width(6)) comparator_2 (.a(in_1), .b(6'b000101), .eq(bne));  // open: gt, lt
  Comparator_part #(.width(6)) comparator_3 (.a(in_1), .b(6'b000110), .eq(blez));  // open: gt, lt
  Comparator_part #(.width(6)) comparator_4 (.a(in_1), .b(6'b000111), .eq(bgtz));  // open: gt, lt
  Comparator_part #(.width(6)) comparator_5 (.a(in_1), .b(6'b000001), .eq(bltz));  // open: gt, lt
  Comparator_part #(.width(6)) comparator_6 (.a(in_1), .b(6'b000010), .eq(j));  // open: gt, lt
  Comparator_part #(.width(6)) comparator_7 (.a(in_1), .b({6{1'b0}}), .eq(comparator_7_eq));  // open: gt, lt
  Comparator_part #(.width(6)) comparator_8 (.a(in_2), .b(6'b001000), .eq(comparator_8_eq));  // open: gt, lt
  and and_1 (jr, comparator_7_eq, comparator_8_eq);

  // Other names for the same wires on the sheet: Func_code[5:0] = in_2; Op_code[5:0] = in_1
endmodule

module RAM_Access (
  input  [31:0] in_1,
  input  [31:0] in_2,
  input  [31:0] in_3,
  input  [31:0] in_4,
  input  [31:0] in_5,
  input  [3:0] in_6,
  input  [3:0] in_7,
  input  in_8,
  input  in_9,
  input  in_10,
  input  in_11,
  input  in_12,
  input  in_13,
  output [15:0] Address,
  output [3:0] Mask,
  output [31:0] RAM_Out,
  output R_W,
  output Chip_Select,
  output Ready_Instruction,
  output Ready_Data,
  output Ready_Write
);

  wire Bip, CS_data, CS_inst, or_1_out;
  wire [31:0] D0, D1, D2, D3, I0, I1, I2, I3, O0, O1, O2, O3;

  Multiplexer #(.width(32)) multiplexer_1 (.in0(D0), .in1(I0), .out(O0), .sel(in_13));  // open: en
  or or_1 (or_1_out, in_8, Bip);
  D_Flip_Flop #(.trigger("falling")) d_ff_1 (.clk(in_9), .D(Bip), .Q(Ready_Write));  // open: Qn, preset, en, reset
  RAM_Read ram_read_1 (
    .in_1(in_2), .in_2(in_3), .in_3(in_4), .in_4(in_5), .in_5(in_6), .in_6(in_11), .in_7(in_9), .in_8(in_10),
    .RAM_O0(I0), .RAM_O1(I1), .RAM_O2(I2), .RAM_O3(I3), .Chip_Select(CS_inst), .Ready(Ready_Instruction));
  D_Flip_Flop #(.trigger("falling")) d_ff_2 (.clk(in_9), .D(in_8), .Q(R_W), .en(or_1_out));  // open: Qn, preset, reset
  Latency latency_1 (.in_1(in_7), .in_2(R_W), .in_3(in_9), .Ready(Bip), .in_4(Ready_Write));
  Multiplexer #(.width(32)) multiplexer_2 (.in0(D1), .in1(I1), .out(O1), .sel(in_13));  // open: en
  Multiplexer #(.width(32)) multiplexer_3 (.in0(D2), .in1(I2), .out(O2), .sel(in_13));  // open: en
  RAM_Read ram_read_2 (
    .in_1(in_2), .in_2(in_3), .in_3(in_4), .in_4(in_5), .in_5(in_6), .in_6(in_12), .in_7(in_9), .in_8(in_10),
    .RAM_O0(D0), .RAM_O1(D1), .RAM_O2(D2), .RAM_O3(D3), .Chip_Select(CS_data), .Ready(Ready_Data));
  Multiplexer #(.width(32)) multiplexer_4 (.in0(D3), .in1(I3), .out(O3), .sel(in_13));  // open: en
  Decoder #(.select(2)) decoder_1 (
    .out0(Mask[0]), .out1(Mask[1]), .out2(Mask[2]), .out3(Mask[3]), .sel(in_1[3:2]));  // open: en
  Multiplexer #(.select(2), .width(32)) multiplexer_5 (
    .in0(O0), .in1(O1), .in2(O2), .in3(O3),
    .out({RAM_Out[7:0], RAM_Out[15:8], RAM_Out[23:16], RAM_Out[31:24]}), .sel(in_1[3:2]));  // open: en
  or or_2 (Chip_Select, R_W, CS_inst, CS_data);

  assign Address = in_1[19:4];

  // Other names for the same wires on the sheet: CLK = in_9; Get_Data = in_12; Get_Inst = in_11; Load_Inst = in_13;
  //   R_W_t = in_8; RAM_O0[31:0] = in_2; RAM_O1[31:0] = in_3; RAM_O2[31:0] = in_4; RAM_O3[31:0] = in_5;
  //   Read_Time[3:0] = in_6; Ready_Inst = Ready_Instruction; RST = in_10; Start = R_W; Target[31:0] = in_1;
  //   Mask_Aux[1:0] = in_1[3:2]; Write_Time[3:0] = in_7
endmodule

module RAM_Read (
  input  [31:0] in_1,
  input  [31:0] in_2,
  input  [31:0] in_3,
  input  [31:0] in_4,
  input  [3:0] in_5,
  input  in_6,
  input  in_7,
  input  in_8,
  output [31:0] RAM_O0,
  output [31:0] RAM_O1,
  output [31:0] RAM_O2,
  output [31:0] RAM_O3,
  output Chip_Select,
  output Ready
);

  wire Bip, en, or_1_out, Start;

  D_Flip_Flop #(.trigger("falling")) d_ff_1 (
    .clk(in_7), .D(in_6), .Q(Start), .en(or_1_out));  // open: Qn, preset, reset
  or or_1 (or_1_out, in_6, Bip);
  Latency latency_1 (.in_1(in_5), .in_2(Start), .in_3(in_7), .Ready(Bip), .in_4(Ready));
  D_Flip_Flop #(.trigger("falling")) d_ff_2 (.clk(in_7), .D(Bip), .Q(en), .reset(Ready));  // open: Qn, preset, en
  D_Flip_Flop #(.trigger("falling")) d_ff_3 (.clk(in_7), .D(en), .Q(Ready));  // open: Qn, preset, en, reset
  Register #(.width(32)) register_1 (.D(in_1), .en(en), .Q(RAM_O0), .clk(in_7), .clr(in_8));
  Register #(.width(32)) register_2 (.D(in_2), .en(en), .Q(RAM_O1), .clk(in_7), .clr(in_8));
  Register #(.width(32)) register_3 (.D(in_3), .en(en), .Q(RAM_O2), .clk(in_7), .clr(in_8));
  Register #(.width(32)) register_4 (.D(in_4), .en(en), .Q(RAM_O3), .clk(in_7), .clr(in_8));
  or or_2 (Chip_Select, Start, en);

  // Other names for the same wires on the sheet: CLK = in_7; Get = in_6; RAM_O0_t[31:0] = in_1; RAM_O1_t[31:0] = in_2;
  //   RAM_O2_t[31:0] = in_3; RAM_O3_t[31:0] = in_4; Read_Time[3:0] = in_5; RST = in_8
endmodule

module Latency (
  input  [3:0] in_1,
  input  in_2,
  input  in_3,
  input  in_4,
  output Ready
);

  wire [3:0] counter_1_q;

  Counter #(.width(4), .max('hf)) counter_1 (
    .count(in_2), .Q(counter_1_q), .clk(in_3), .clr(in_4));  // open: load, D, carry
  Comparator_part #(.width(4)) comparator_1 (.a(in_1), .b(counter_1_q), .eq(Ready));  // open: gt, lt

  // Other names for the same wires on the sheet: CLK = in_3; RST = in_4; Start = in_2; Time[3:0] = in_1
endmodule
